# Fritzing sketch StubeToGo (saved by Fritzing 0.8.3b)
perfboards: 1

parts:
  T1 = LM35 Temperature Sensor [package="TO92 [THT]"]  # not connected
  S1 = Round Pushbutton  # not connected
  Bauteil1 = Arduino Uno (Rev3)  # not connected
  LED1 = LED - 5mm [color="Blue (505nm)" package="5 mm [THT]"]
  LED2 = LED - 5mm [color="Red (633nm)" package="5 mm [THT]"]  # not connected
  LED3 = LED - 5mm [color="Green (570nm)" package="5 mm [THT]"]
  R1 = Resistor [tolerance=±5% resistance=10k package=THT]  # not connected
  T2 = LM35 Temperature Sensor [package="TO92 [THT]"]  # not connected
  Bauteil3 = Arduino Prototyping Shield  # not connected

nets:
  N1: LED1.cathode, LED3.cathode

notes:
  5V - GND
  A0 A1
  06 05 - 03 02
